# Fritzing sketch CP2102-circuit (saved by Fritzing 0.9.3b)

parts:
  Raspberry_Pi_1 = Raspberry Pi 3 [part_number=RPI-3-V1.2]
  U3 = TTL UART CP2102

nets:
  N1: Raspberry_Pi_1.GPIO15, U3.TXD
  N2: Raspberry_Pi_1.GPIO14, U3.RXD
  GND: Raspberry_Pi_1.GND, U3.GND

custom parts:
  TTL UART CP2102: 6Pin USB 2.0 to TTL UART Module Serial Converter CP2102 STC Replace Ft232 Module
