# Fritzing sketch YL-69-soil (saved by Fritzing 0.9.3b)
breadboards: 1

parts:
  Part5 = FC-28 Soil Hygrometer Module
  Part1 = Arduino Uno (Rev3)
  Part6 = FC-28 Soil Hygrometer Module - Probe

nets:
  VCC: Part5.VCC, Part1.5V
  GND: Part5.GND, Part1.GND
  N1: Part5.AO, Part1.A0
  N2: Part5.POS, Part6.POS
  N3: Part5.NEG, Part6.NEG

custom parts:
  FC-28 Soil Hygrometer Module: The FC-28 is a soil hygrometer module that uses the Texas Instruments LM393 comparator chip to provide an analog measurement of soil humidity. The digital output is high when soil moisture is over a certain threshold, as determined by adjusting the potentiometer.
  FC-28 Soil Hygrometer Module - Probe: The FC-28 is a soil hygrometer module that uses the Texas Instruments LM393 comparator chip to provide an analog measurement of soil humidity.
