# Fritzing sketch temp-light-sensor (saved by Fritzing 0.9.3b)
breadboards: 1

parts:
  Part1 = Arduino Uno (Rev3)
  DS1 = DS18B20 1-Wire Temperature Sensor [part_number=DS18B20]
  R1 = Resistor [tolerance=±5% resistance=4.7k package="1206 [SMD]"]
  R2 = PHOTOCELL [package=photocell-kit]
  R3 = Resistor [tolerance=±5% resistance=10k package="2010 [SMD]"]

nets:
  N1: Part1.A1, R2.P$2, R3.Pin_0
  N2: Part1.D2, DS1.DQ, R1.Pin_0
  5V: Part1.5V, DS1.VDD, R1.Pin_1, R3.Pin_1
  GND: Part1.GND, DS1.GND, R2.P$1
